// Logisim project dip8.circ as structural Verilog: 14 circuits, main circuit main
module main (
);

  wire and_1_out, and_2_out, aout, BHWR, BLWR, CarryFlag, CHWR, CK1, CK2, CLEAR_out, clock_1_out, CLWR,
       decoder_1_out0, decoder_1_out1, decoder_1_out2, decoder_1_out3, irwr, n74x138_decoder_2_y0,
       n74x138_decoder_2_y1, n74x138_decoder_2_y2, n74x138_decoder_2_y3, n74x138_decoder_2_y4,
       n74x138_decoder_2_y5, n74x138_decoder_2_y6, n74x138_decoder_2_y7, nahwr, nainc, nalu, nalwr,
       nand_1_out, nBHOE, nBLOE, nBRK, nCHOE, nCLOE, NegFlag, nmemrd, nmemwr, nnext, not_1_out, not_3_out,
       not_4_out, not_5_out, npcinc, npcwr, nregoe, nregwr, nsetflags, nshoe, nsloe, nxoe, nyoe, or_2_out,
       periphsel, ramsel, RESET, romsel, shwr, slwr, Step_Resume_out, tclk, twr, xwr, ywr, ZeroFlag;
  wire [2:0] regsel;
  wire [3:0] counter_1_q, opsel, pc_1_addr_2;
  wire [6:0] controlled_buffer_2_out;
  wire [7:0] bhval, blval, chval, clval, controlled_buffer_1_out, INST, reg8lr_1_q, rom_1_data, shval, slval,
       t_q, tval, xval, yval;
  wire [7:7] controlled_buffer_2_out_2;
  wire [11:0] pc_1_addr;
  wire [15:0] aval;
  wire [31:23] rom_2_data;

  Button u_RESET (.out(RESET));
  LED Halted (.in(not_1_out));
  Button Step_Resume (.out(Step_Resume_out));
  Clock clock_1 (.out(clock_1_out));
  // Probe on tval
  // Probe on aval
  // Probe on bhval
  // Probe on blval
  // Probe on chval
  // Probe on clval
  // Probe on xval
  // Probe on yval
  // Probe on shval
  // Probe on slval
  not not_1 (not_1_out, nBRK);
  and and_1 (and_1_out, clock_1_out, nBRK);
  or or_1 (CK1, Step_Resume_out, and_1_out);
  not not_2 (CK2, CK1);
  LED u_CK1 (.in(CK1));
  LED u_CK2 (.in(CK2));
  // Probe on {controlled_buffer_2_out_2[7], controlled_buffer_2_out}
  // Probe on {pc_1_addr_2, pc_1_addr}
  TTY tty_1 (.data(controlled_buffer_2_out), .clk(CK2), .we(periphsel), .clr(RESET));
  or or_2 (or_2_out, nmemwr, CK1);
  Decoder #(.select(4), .disabled(0), .enable("false")) decoder_1 (
    .out0(decoder_1_out0), .out1(decoder_1_out1), .out2(decoder_1_out2), .out3(decoder_1_out3),
    .out15(periphsel), .sel(pc_1_addr_2));  // open: out4, out5, out6, out7, out8, out9, out10, out11, out12, out13, out14
  ROM #(.addrWidth(16)) rom_1 (.addr({pc_1_addr_2, pc_1_addr}), .data(rom_1_data), .sel(romsel));
  and and_2 (and_2_out, romsel, not_3_out);
  assign controlled_buffer_1_out = nmemrd ? {controlled_buffer_2_out_2[7], controlled_buffer_2_out} : 8'bz;  // Controlled_Buffer controlled_buffer_1
  RAM #(.addrWidth(16), .bus("asynch")) ram_1 (
    .addr({pc_1_addr_2, pc_1_addr}), .data(controlled_buffer_1_out), .sel(ramsel), .ld(or_2_out),
    .clr(CLEAR_out));
  not not_3 (not_3_out, nmemrd);
  Button CLEAR (.out(CLEAR_out));
  or or_3 (romsel, decoder_1_out0, decoder_1_out1, decoder_1_out2, decoder_1_out3);
  assign {controlled_buffer_2_out_2[7], controlled_buffer_2_out} = and_2_out ? rom_1_data : 8'bz;  // Controlled_Buffer controlled_buffer_2
  assign {controlled_buffer_2_out_2[7], controlled_buffer_2_out} = not_3_out ? controlled_buffer_1_out : 8'bz;  // Controlled_Buffer controlled_buffer_3
  nor nor_1 (ramsel, romsel, periphsel);
  Register register_1 (
    .D({controlled_buffer_2_out_2[7], controlled_buffer_2_out}), .en(irwr), .Q(INST), .clk(CK1), .clr(RESET));
  reg8LR reg8lr_1 (
    .D({controlled_buffer_2_out_2[7], controlled_buffer_2_out}), .Rst(RESET), .View(bhval), .Q(reg8lr_1_q),
    .Clk(BHWR), .nOE(nBHOE));
  reg8LR reg8lr_2 (
    .D({controlled_buffer_2_out_2[7], controlled_buffer_2_out}), .Rst(RESET), .View(xval), .Q(reg8lr_1_q),
    .Clk(xwr), .nOE(nxoe));
  pc pc_1 (
    .DL(pc_1_addr[7:0]), .DH({pc_1_addr_2, pc_1_addr[11:8]}), .Clk(CK1), .Rst(RESET), .nPCNext(npcinc),
    .nWR(npcwr), .nOE(aout), .Addr({pc_1_addr_2, pc_1_addr}));
  not not_4 (not_4_out, RESET);
  not not_5 (not_5_out, aout);
  Counter #(.width(4), .max('hf)) counter_1 (
    .count(1'b1), .Q(counter_1_q), .clk(CK1), .clr(nand_1_out));  // open: load, D, carry
  nand nand_1 (nand_1_out, not_4_out, nnext);
  reg8LR reg8lr_3 (
    .D({controlled_buffer_2_out_2[7], controlled_buffer_2_out}), .Rst(RESET), .View(blval), .Q(reg8lr_1_q),
    .Clk(BLWR), .nOE(nBLOE));
  reg8LR reg8lr_4 (
    .D({controlled_buffer_2_out_2[7], controlled_buffer_2_out}), .Rst(RESET), .View(yval), .Q(reg8lr_1_q),
    .Clk(ywr), .nOE(nyoe));
  // Probe on counter_1_q
  // Probe on INST
  reg8LR reg8lr_5 (
    .D({controlled_buffer_2_out_2[7], controlled_buffer_2_out}), .Rst(RESET), .View(chval), .Q(reg8lr_1_q),
    .Clk(CHWR), .nOE(nCHOE));
  reg8LR reg8lr_6 (
    .D({controlled_buffer_2_out_2[7], controlled_buffer_2_out}), .Rst(RESET), .View(shval), .Q(reg8lr_1_q),
    .Clk(shwr), .nOE(nshoe));
  _16BitCtrRegister u_16bitctrregister_1 (
    .Clk(CK2), .Rst(RESET), .ninc(nainc), .nLWR(nalwr), .nHWR(nahwr), .noe(not_5_out),
    .DL({controlled_buffer_2_out_2[7], controlled_buffer_2_out}),
    .DH({controlled_buffer_2_out_2[7], controlled_buffer_2_out}), .Addr({pc_1_addr_2, pc_1_addr}), .View(aval));
  _74x138_decoder u_74x138_decoder_1 (
    .G1(1'b1), .nG2A(1'b0), .nG2B(nregoe), .SEL(regsel), .Y0(nBHOE), .Y1(nBLOE), .Y2(nCHOE), .Y3(nCLOE),
    .Y4(nxoe), .Y5(nyoe), .Y6(nshoe), .Y7(nsloe));
  _74x138_decoder u_74x138_decoder_2 (
    .G1(1'b1), .nG2A(CK1), .nG2B(nregwr), .SEL(regsel), .Y0(n74x138_decoder_2_y0), .Y1(n74x138_decoder_2_y1),
    .Y2(n74x138_decoder_2_y2), .Y3(n74x138_decoder_2_y3), .Y4(n74x138_decoder_2_y4),
    .Y5(n74x138_decoder_2_y5), .Y6(n74x138_decoder_2_y6), .Y7(n74x138_decoder_2_y7));
  not not_6 (BHWR, n74x138_decoder_2_y0);
  not not_7 (BLWR, n74x138_decoder_2_y1);
  not not_8 (CHWR, n74x138_decoder_2_y2);
  not not_9 (CLWR, n74x138_decoder_2_y3);
  not not_10 (xwr, n74x138_decoder_2_y4);
  not not_11 (ywr, n74x138_decoder_2_y5);
  not not_12 (shwr, n74x138_decoder_2_y6);
  not not_13 (slwr, n74x138_decoder_2_y7);
  reg8LR reg8lr_7 (
    .D({controlled_buffer_2_out_2[7], controlled_buffer_2_out}), .Rst(RESET), .View(clval), .Q(reg8lr_1_q),
    .Clk(CLWR), .nOE(nCLOE));
  reg8LR reg8lr_8 (
    .D({controlled_buffer_2_out_2[7], controlled_buffer_2_out}), .Rst(RESET), .View(slval), .Q(reg8lr_1_q),
    .Clk(slwr), .nOE(nsloe));
  ROM #(.addrWidth(16), .dataWidth(32)) rom_2 (
    .addr({1'b0, NegFlag, ZeroFlag, CarryFlag, INST, counter_1_q}),
    .data({rom_2_data, nBRK, nsetflags, twr, nalu, nainc, nregwr, nregoe, nalwr, nahwr, regsel, opsel, nmemwr, nmemrd, irwr, npcwr, npcinc, aout, nnext}));  // open: sel
  reg8LR t (
    .D({controlled_buffer_2_out_2[7], controlled_buffer_2_out}), .Rst(RESET), .View(tval), .Q(t_q),
    .Clk(tclk), .nOE(1'b0));
  and and_3 (tclk, CK2, twr);
  alu alu_1 (
    .A(reg8lr_1_q), .B(t_q), .opsel(opsel), .nsetflags(nsetflags), .cout(CarryFlag), .z(ZeroFlag),
    .n(NegFlag), .noe(nalu), .reset(RESET), .clk(CK2),
    .Q({controlled_buffer_2_out_2[7], controlled_buffer_2_out}));

  // Notes on the sheet:
  //   contents of rom_1 (hex, n*v repeats v):
  //   6d 5 0 9*f6 ff
  //   contents of rom_2 (hex, n*v repeats v):
  //   6fc059 6f4049 6f8049 13*6fc06c 6fc059 66486d 66806d 13*6fc06c 6fc059 66586d 66906d 13*6fc06c 6fc059
  //   66786d 66b06d 13*6fc06c 6fc059 7fc049 66496d 6684ed 12*6fc06c 6fc059 7fc049 66596d 6694ed 12*6fc06c
  //   6fc059 7fc049 66796d 66b4ed 12*6fc06c 6fc059 7fc049 66496d 7fc049 66826d 11*6fc06c 6fc059 7fc049
  //   66596d 7fc049 66926d 11*6fc06c 6fc059 7fc049 66796d 7fc049 66b26d 11*6fc06c 6fc059 76e06d 66496d
  //   6684ed 12*6fc06c 6fc059 76e06d 66596d 6694ed 12*6fc06c 6fc059 76e06d 66796d 66b4ed 12*6fc06c 6fc059
  //   76e86d 66496d 6684ed 12*6fc06c 6fc059 76e86d 66596d 6694ed 12*6fc06c 6fc059 76e86d 66796d 66b4ed
  //   12*6fc06c 6fc059 76f86d 66496d 76f06d 66826d 11*6fc06c 6fc059 76f86d 66596d 76f06d 66926d 11*6fc06c
  //   6fc059 76c86d 66596d 76c06d 6694ed 11*6fc06c 6fc059 7bc04f 6f804f 6740ed 12*6fc06c 6fc059 6f4049
  //   6f8049 6fc067 12*6fc06c 6fc059 6fc067 14*6fc06c 6fc059 6f4049 6f8049 13*6fc06c 6fc059 15*6fc06c
  //   6fc059 6f4049 6f8049 6fc067 12*6fc06c 6fc059 6fc067 14*6fc06c 6fc059 6f4049 6f8049 13*6fc06c 6fc059
  //   15*6fc06c 6fc059 6f4049 6f8049 6fc067 12*6fc06c 6fc059 6fc067 14*6fc06c 6fc059 647d6d 64b4ed 7fc04f
  //   647d6d 64b4ed 6f804f 6740ed 6fc067 7*6fc06c 6fc059 7fc049 67c0af 13*6fc06c 6fc059 6de04f 14*6fc06c
  //   6fc059 6de84f 14*6fc06c 6fc059 69c84f 6dc04f 13*6fc06c 6fc059 69d84f 6dd04f 13*6fc06c 6fc059 6dc04f
  //   14*6fc06c 6fc059 6dc84f 14*6fc06c 6fc059 6dd04f 14*6fc06c 6fc059 6dd84f 14*6fc06c 6fc059 66e02f
  //   14*6fc06c 6fc059 66e82f 14*6fc06c 6fc059 62c82f 66c02f 13*6fc06c 6fc059 62d82f 66d02f 13*6fc06c
  //   6fc059 66c02f 14*6fc06c 6fc059 66c82f 14*6fc06c 6fc059 66d02f 14*6fc06c 6fc059 66d82f 14*6fc06c
  //   6fc059 66786d 66b06d 66e02f 64fded 64f66d 10*6fc06c 6fc059 66786d 66b06d 66e82f 64fded 64f66d
  //   10*6fc06c 6fc059 66786d 66b06d 66c02f 647ded 64b66d 66c82f 64fded 64f66d 7*6fc06c 6fc059 66786d
  //   66b06d 66d02f 647ded 64b66d 66d82f 64fded 64f66d 7*6fc06c 6fc059 647d6d 64b4ed 66e02f 12*6fc06c
  //   6fc059 647d6d 64b4ed 66e82f 12*6fc06c 6fc059 647d6d 64b4ed 66c82f 647d6d 64b4ed 66c02f 9*6fc06c
  //   6fc059 647d6d 64b4ed 66d82f 647d6d 64b4ed 66d02f 9*6fc06c 6fc059 7fc049 66786d 66b06d 67c0af 7fc049
  //   647ded 64b66d 67c0af 647ded 64b66d 5*6fc06c 6fc059 76c86d 65f8ed 76c06d 65f0ed 11*6fc06c 6fc059
  //   76d86d 65f8ed 76d06d 65f0ed 11*6fc06c 6fc059 76f86d 65c8ed 76f06d 65c0ed 11*6fc06c 6fc059 76f86d
  //   65d8ed 76f06d 65d0ed 11*6fc06c 48*0 6fc059 6dc049 14*6fc06c 6fc059 76c86d 65c0ed 13*6fc06c 6fc059
  //   76d06d 65c0ed 13*6fc06c 6fc059 76d86d 65c0ed 13*6fc06c 6fc059 76e06d 65c0ed 13*6fc06c 6fc059 76e86d
  //   65c0ed 13*6fc06c 6fc059 76c06d 65c8ed 13*6fc06c 6fc059 6dc849 14*6fc06c 6fc059 76d06d 65c8ed
  //   13*6fc06c 6fc059 76d86d 65c8ed 13*6fc06c 6fc059 76e06d 65c8ed 13*6fc06c 6fc059 76e86d 65c8ed
  //   13*6fc06c 6fc059 76c06d 65d0ed 13*6fc06c 6fc059 76c86d 65d0ed 13*6fc06c 6fc059 6dd049 14*6fc06c
  //   6fc059 76d86d 65d0ed 13*6fc06c 6fc059 76e06d 65d0ed 13*6fc06c 6fc059 76e86d 65d0ed 13*6fc06c 6fc059
  //   76c06d 65d8ed 13*6fc06c 6fc059 76c86d 65d8ed 13*6fc06c 6fc059 76d06d 65d8ed 13*6fc06c 6fc059 6dd849
  //   14*6fc06c 6fc059 76e06d 65d8ed 13*6fc06c 6fc059 76e86d 65d8ed 13*6fc06c 6fc059 76c06d 65e0ed
  //   13*6fc06c 6fc059 76c86d 65e0ed 13*6fc06c 6fc059 76d06d 65e0ed 13*6fc06c 6fc059 76d86d 65e0ed
  //   13*6fc06c 6fc059 6de049 14*6fc06c 6fc059 76e86d 65e0ed 13*6fc06c 6fc059 76c06d 65e8ed 13*6fc06c
  //   6fc059 76c86d 65e8ed 13*6fc06c 6fc059 76d06d 65e8ed 13*6fc06c 6fc059 76d86d 65e8ed 13*6fc06c 6fc059
  //   76e06d 65e8ed 13*6fc06c 6fc059 6de849 14*6fc06c 6fc059 76c06d 14*6fc06c 6fc059 76c86d 14*6fc06c
  //   6fc059 76d06d 14*6fc06c 6fc059 76d86d 14*6fc06c 6fc059 76e06d 14*6fc06c 6fc059 76e86d 14*6fc06c
  //   6fc059 7fc049 14*6fc06c 6fc059 76d86d 65c8ed 76d06d 65c0ed 11*6fc06c 6fc059 76c86d 65d8ed 76c06d
  //   65d0ed 11*6fc06c 6fc059 6dc849 6dc049 13*6fc06c 6fc059 6dd849 6dd049 13*6fc06c 6fc059 7fc04f
  //   14*6fc06c 6fc059 44e16d 14*6fc06c 6fc059 7fc049 44e16d 13*6fc06c 6fc059 44e96d 14*6fc06c 6fc059
  //   7fc049 44e96d 13*6fc06c 6fc059 44c16d 14*6fc06c 6fc059 7fc049 44c16d 13*6fc06c 6fc059 44c96d
  //   14*6fc06c 6fc059 7fc049 44c96d 13*6fc06c 6fc059 44d16d 14*6fc06c 6fc059 7fc049 44d16d 13*6fc06c
  //   6fc059 44d96d 14*6fc06c 6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
endmodule

// A
module _16BitCtrRegister (
  input  [7:0] DL,
  input  [7:0] DH,
  input  Clk,
  input  Rst,
  input  ninc,
  input  nLWR,
  input  nHWR,
  input  noe,
  output [15:0] View,
  output [15:0] Addr
);

  wire n74x469_counter_1_ncbo, not_1_out, or_1_out;

  // Probe on DL
  _74x469_counter u_74x469_counter_1 (
    .D(DL), .nUD(1'b0), .nCBI(ninc), .nLD(nLWR), .CK(Clk), .Rst(Rst), .nOE(1'b0),
    .nCBO(n74x469_counter_1_ncbo), .Q(View[7:0]));
  // Probe on DH
  or or_1 (or_1_out, n74x469_counter_1_ncbo, ninc);
  _74x469_counter u_74x469_counter_2 (
    .D(DH), .nUD(1'b0), .nCBI(or_1_out), .nLD(nHWR), .CK(Clk), .Rst(Rst), .nOE(1'b0), .Q(View[15:8]));  // open: nCBO
  // Probe on View
  not not_1 (not_1_out, noe);
  assign Addr = not_1_out ? View : 16'bz;  // Controlled_Buffer controlled_buffer_1
endmodule

module _74x469_counter (
  input  [7:0] D,
  input  nUD,
  input  nCBI,
  input  nLD,
  input  CK,
  input  Rst,
  input  nOE,
  output [7:0] Q,
  output nCBO
);

  wire and_1_out, and_2_out, counter_1_carry, not_1_out, not_2_out, not_3_out, or_1_out;
  wire [7:0] counter_1_q;

  not not_1 (not_1_out, nCBI);
  and and_1 (and_1_out, nUD, not_1_out, nLD);
  not not_2 (not_2_out, nLD);
  or or_1 (or_1_out, and_1_out, not_2_out);
  and and_2 (and_2_out, not_1_out, nLD);
  assign Q = not_3_out ? counter_1_q : 8'bz;  // Controlled_Buffer controlled_buffer_1
  Counter counter_1 (
    .load(or_1_out), .D(D), .count(and_2_out), .Q(counter_1_q), .carry(counter_1_carry), .clk(CK), .clr(Rst));
  not not_3 (not_3_out, nOE);
  not not_4 (nCBO, counter_1_carry);
endmodule

module _74x181_ALU (
  input  [3:0] S,
  input  [3:0] A,
  input  [3:0] B,
  input  M,
  input  Cn,
  output Cn_4,
  output [3:0] F,
  output A_B
);

  wire and_1_out, and_2_out, and_3_out, and_4_out, and_5_out, and_6_out, and_7_out, and_8_out, and_9_out,
       and_10_out, and_11_out, and_12_out, and_13_out, and_14_out, and_15_out, and_16_out, and_17_out,
       and_18_out, and_19_out, and_20_out, and_21_out, and_22_out, and_23_out, and_24_out, and_25_out,
       and_26_out, and_27_out, and_28_out, and_29_out, and_30_out, and_31_out, and_32_out, buffer_1_out,
       buffer_2_out, buffer_3_out, buffer_4_out, buffer_5_out, nand_1_out, nand_2_out, nand_3_out, nor_1_out,
       nor_2_out, nor_3_out, nor_4_out, nor_5_out, nor_6_out, nor_7_out, nor_8_out, nor_9_out, nor_10_out,
       nor_11_out, nor_12_out, not_1_out, not_2_out, not_3_out, not_4_out, not_5_out, not_6_out, not_7_out,
       not_8_out, not_9_out;

  not not_1 (not_1_out, M);
  not not_2 (not_2_out, B[3]);
  not not_3 (not_3_out, B[2]);
  not not_4 (not_4_out, B[1]);
  not not_5 (not_5_out, B[0]);
  and and_1 (and_1_out, B[3], S[3], A[3]);
  and and_2 (and_2_out, A[3], S[2], not_2_out);
  and and_3 (and_3_out, not_2_out, S[1]);
  and and_4 (and_4_out, S[0], B[3]);
  buf buffer_1 (buffer_1_out, A[3]);
  and and_5 (and_5_out, B[2], S[3], A[2]);
  and and_6 (and_6_out, A[2], S[2], not_3_out);
  and and_7 (and_7_out, not_3_out, S[1]);
  and and_8 (and_8_out, S[0], B[2]);
  buf buffer_2 (buffer_2_out, A[2]);
  and and_9 (and_9_out, B[1], S[3], A[1]);
  and and_10 (and_10_out, A[1], S[2], not_4_out);
  and and_11 (and_11_out, not_4_out, S[1]);
  and and_12 (and_12_out, S[0], B[1]);
  buf buffer_3 (buffer_3_out, A[1]);
  and and_13 (and_13_out, B[0], S[3], A[0]);
  and and_14 (and_14_out, A[0], S[2], not_5_out);
  and and_15 (and_15_out, not_5_out, S[1]);
  and and_16 (and_16_out, S[0], B[0]);
  buf buffer_4 (buffer_4_out, A[0]);
  nor nor_1 (nor_1_out, and_1_out, and_2_out);
  nor nor_2 (nor_2_out, and_3_out, and_4_out, buffer_1_out);
  nor nor_3 (nor_3_out, and_5_out, and_6_out);
  nor nor_4 (nor_4_out, and_7_out, and_8_out, buffer_2_out);
  nor nor_5 (nor_5_out, and_9_out, and_10_out);
  nor nor_6 (nor_6_out, and_11_out, and_12_out, buffer_3_out);
  nor nor_7 (nor_7_out, and_13_out, and_14_out);
  nor nor_8 (nor_8_out, and_15_out, and_16_out, buffer_4_out);
  buf buffer_5 (buffer_5_out, nor_2_out);
  and and_17 (and_17_out, nor_1_out, nor_4_out);
  and and_18 (and_18_out, nor_1_out, nor_3_out, nor_6_out);
  and and_19 (and_19_out, nor_1_out, nor_3_out, nor_5_out, nor_8_out);
  nand nand_1 (nand_1_out, nor_1_out, nor_3_out, nor_5_out, nor_7_out, Cn);
  nand nand_2 (nand_2_out, nor_1_out, nor_3_out, nor_5_out, nor_7_out);
  not not_6 (not_6_out, nor_2_out);
  and and_20 (and_20_out, nor_3_out, nor_5_out, nor_7_out, Cn, not_1_out);
  and and_21 (and_21_out, nor_3_out, nor_5_out, nor_8_out, not_1_out);
  and and_22 (and_22_out, nor_3_out, nor_6_out, not_1_out);
  and and_23 (and_23_out, nor_4_out, not_1_out);
  not not_7 (not_7_out, nor_4_out);
  and and_24 (and_24_out, nor_5_out, nor_7_out, Cn, not_1_out);
  and and_25 (and_25_out, nor_5_out, nor_8_out, not_1_out);
  and and_26 (and_26_out, nor_6_out, not_1_out);
  not not_8 (not_8_out, nor_6_out);
  and and_27 (and_27_out, Cn, nor_7_out, not_1_out);
  and and_28 (and_28_out, nor_8_out, not_1_out);
  not not_9 (not_9_out, nor_8_out);
  nand nand_3 (nand_3_out, not_1_out, Cn);
  nor nor_9 (nor_9_out, buffer_5_out, and_17_out, and_18_out, and_19_out);
  and and_29 (and_29_out, nor_1_out, not_6_out);
  nor nor_10 (nor_10_out, and_20_out, and_21_out, and_22_out, and_23_out);
  and and_30 (and_30_out, nor_3_out, not_7_out);
  nor nor_11 (nor_11_out, and_24_out, and_25_out, and_26_out);
  and and_31 (and_31_out, nor_5_out, not_8_out);
  nor nor_12 (nor_12_out, and_27_out, and_28_out);
  and and_32 (and_32_out, nor_7_out, not_9_out);
  or or_1 (Cn_4, ~nor_9_out, ~nand_1_out);  // OR_Gate
  xor xor_1 (F[3], and_29_out, nor_10_out);
  xor xor_2 (F[2], and_30_out, nor_11_out);
  xor xor_3 (F[1], and_31_out, nor_12_out);
  xor xor_4 (F[0], and_32_out, nand_3_out);
  and and_33 (A_B, F[3], F[2], F[1], F[0]);

  // Notes on the sheet:
  //   Carry propagate
  //   Carry generate
endmodule

module _74x138_decoder (
  input  G1,
  input  nG2A,
  input  nG2B,
  input  [2:0] SEL,
  output Y0,
  output Y1,
  output Y2,
  output Y3,
  output Y4,
  output Y5,
  output Y6,
  output Y7
);

  wire and_1_out, decoder_1_out0, decoder_1_out1, decoder_1_out2, decoder_1_out3, decoder_1_out4,
       decoder_1_out5, decoder_1_out6, decoder_1_out7, not_1_out;

  not not_1 (not_1_out, G1);
  and and_1 (and_1_out, ~not_1_out, ~nG2A, ~nG2B);  // AND_Gate
  Decoder #(.select(3), .disabled(0)) decoder_1 (
    .out0(decoder_1_out0), .out1(decoder_1_out1), .out2(decoder_1_out2), .out3(decoder_1_out3),
    .out4(decoder_1_out4), .out5(decoder_1_out5), .out6(decoder_1_out6), .out7(decoder_1_out7), .sel(SEL),
    .en(and_1_out));
  not not_2 (Y0, decoder_1_out0);
  not not_3 (Y2, decoder_1_out2);
  not not_4 (Y4, decoder_1_out4);
  not not_5 (Y6, decoder_1_out6);
  not not_6 (Y1, decoder_1_out1);
  not not_7 (Y3, decoder_1_out3);
  not not_8 (Y5, decoder_1_out5);
  not not_9 (Y7, decoder_1_out7);
endmodule

module RAMController (
  input  [7:0] RAMin,
  input  [7:0] BUSin,
  input  Clk,
  input  nWR,
  input  nOE,
  output nWE,
  output [7:0] RAMout,
  output [7:0] BUSout
);

  wire not_1_out, not_2_out, not_3_out, or_1_out;

  or or_1 (or_1_out, Clk, not_1_out);
  not not_1 (not_1_out, Clk);
  or or_2 (nWE, or_1_out, nWR);
  assign RAMout = not_2_out ? BUSin : 8'bz;  // Controlled_Buffer controlled_buffer_1
  not not_2 (not_2_out, nWR);
  assign BUSout = not_3_out ? RAMin : 8'bz;  // Controlled_Buffer controlled_buffer_2
  not not_3 (not_3_out, nOE);
endmodule

module _74x374_ff (
  input  [7:0] D,
  input  Clk,
  input  Rst,
  input  nOC,
  output [7:0] View,
  output [7:0] Q
);

  wire not_1_out;

  Register register_1 (.D(D), .en(1'b1), .Q(View), .clk(Clk), .clr(Rst));
  assign Q = not_1_out ? View : 8'bz;  // Controlled_Buffer controlled_buffer_1
  not not_1 (not_1_out, nOC);
endmodule

module _74x139 (
  input  E,
  input  [1:0] SEL,
  output Y0,
  output Y1,
  output Y2,
  output Y3
);

  wire decoder_1_out0, decoder_1_out1, decoder_1_out2, decoder_1_out3, not_1_out;

  not not_1 (not_1_out, E);
  Decoder #(.select(2), .disabled(0)) decoder_1 (
    .out0(decoder_1_out0), .out1(decoder_1_out1), .out2(decoder_1_out2), .out3(decoder_1_out3), .sel(SEL),
    .en(not_1_out));
  not not_2 (Y0, decoder_1_out0);
  not not_3 (Y2, decoder_1_out2);
  not not_4 (Y1, decoder_1_out1);
  not not_5 (Y3, decoder_1_out3);
endmodule

module _74x157 (
  input  [3:0] A,
  input  [3:0] B,
  input  Select,
  input  Strobe,
  output [3:0] out
);

  wire not_1_out;

  Multiplexer #(.width(4), .disabled(0)) multiplexer_1 (.in0(A), .in1(B), .out(out), .sel(Select), .en(not_1_out));
  not not_1 (not_1_out, Strobe);
endmodule

module _74x541_buffer (
  input  [7:0] D,
  input  nOE,
  output [7:0] Q
);

  wire not_1_out;

  assign Q = not_1_out ? D : 8'bz;  // Controlled_Buffer controlled_buffer_1
  not not_1 (not_1_out, nOE);
endmodule

module reg8LR (
  input  [7:0] D,
  input  Clk,
  input  Rst,
  input  nOE,
  output [7:0] View,
  output [7:0] Q
);

  _74x374_ff u_74x374_ff_1 (.View(View), .D(D), .Q(Q), .Clk(Clk), .Rst(Rst), .nOC(nOE));
endmodule

// PC
module pc (
  input  [7:0] DL,
  input  [7:0] DH,
  input  Clk,
  input  Rst,
  input  nPCNext,
  input  nWR,
  input  nOE,
  output [15:0] Addr
);

  wire and_1_out, and_2_out, counter_1_carry, not_1_out, not_2_out, not_3_out;
  wire [7:0] counter_1_q, counter_2_q;

  and and_1 (and_1_out, nWR, not_2_out);
  not not_1 (not_1_out, nWR);
  not not_2 (not_2_out, nPCNext);
  Counter counter_1 (
    .load(not_1_out), .D(DL), .count(and_1_out), .Q(counter_1_q), .carry(counter_1_carry), .clk(Clk),
    .clr(Rst));
  and and_2 (and_2_out, counter_1_carry, and_1_out);
  Counter counter_2 (
    .load(not_1_out), .D(DH), .count(and_2_out), .Q(counter_2_q), .clk(Clk), .clr(Rst));  // open: carry
  not not_3 (not_3_out, nOE);
  assign Addr = not_3_out ? {counter_2_q, counter_1_q} : 16'bz;  // Controlled_Buffer controlled_buffer_1
endmodule

// ALU
module alu (
  input  nsetflags,
  input  [3:0] opsel,
  input  noe,
  input  reset,
  input  clk,
  input  [7:0] A,
  input  [7:0] B,
  output cout,
  output z,
  output n,
  output [7:0] Q
);

  wire and_1_out, not_1_out;
  wire [7:0] rom_1_data, rom_2_data;
  wire [13:13] ffwithenable_1_q;

  Pull_Resistor pull_resistor_1 (.node(A));
  ROM #(.addrWidth(16)) rom_1 (
    .addr({1'b0, cout, ffwithenable_1_q[13], opsel, nsetflags, B[3:0], A[3:0]}), .data(rom_1_data), .sel(1'b1));
  ROM #(.addrWidth(16)) rom_2 (
    .addr({1'b1, {2{rom_1_data[4]}}, opsel, nsetflags, B[7:4], A[7:4]}), .data(rom_2_data), .sel(1'b1));
  and and_1 (and_1_out, rom_1_data[5], rom_2_data[5]);
  not not_1 (not_1_out, noe);
  assign Q = not_1_out ? {rom_2_data[3:0], rom_1_data[3:0]} : 8'bz;  // Controlled_Buffer controlled_buffer_1
  FFwithEnable ffwithenable_1 (
    .D(rom_2_data[4]), .nen(rom_1_data[7]), .Clk(clk), .Rst(reset), .Q(ffwithenable_1_q[13]));
  FFwithEnable ffwithenable_2 (.D(rom_2_data[4]), .nen(rom_2_data[7]), .Clk(clk), .Rst(reset), .Q(cout));
  FFwithEnable ffwithenable_3 (.D(and_1_out), .nen(rom_2_data[7]), .Clk(clk), .Rst(reset), .Q(z));
  FFwithEnable ffwithenable_4 (.D(rom_2_data[6]), .nen(rom_2_data[7]), .Clk(clk), .Rst(reset), .Q(n));

  // Notes on the sheet:
  //   LOW
  //   contents of rom_1 (hex, n*v repeats v):
  //   a0 81 82 83 84 85 86 87 c8 c9 ca cb cc cd ce cf a0 81 82 83 84 85 86 87 c8 c9 ca cb cc cd ce cf a0
  //   81 82 83 84 85 86 87 c8 c9 ca cb cc cd ce cf a0 81 82 83 84 85 86 87 c8 c9 ca cb cc cd ce cf a0 81
  //   82 83 84 85 86 87 c8 c9 ca cb cc cd ce cf a0 81 82 83 84 85 86 87 c8 c9 ca cb cc cd ce cf a0 81 82
  //   83 84 85 86 87 c8 c9 ca cb cc cd ce cf a0 81 82 83 84 85 86 87 c8 c9 ca cb cc cd ce cf a0 81 82 83
  //   84 85 86 87 c8 c9 ca cb cc cd ce cf a0 81 82 83 84 85 86 87 c8 c9 ca cb cc cd ce cf a0 81 82 83 84
  //   85 86 87 c8 c9 ca cb cc cd ce cf a0 81 82 83 84 85 86 87 c8 c9 ca cb cc cd ce cf a0 81 82 83 84 85
  //   86 87 c8 c9 ca cb cc cd ce cf a0 81 82 83 84 85 86 87 c8 c9 ca cb cc cd ce cf a0 81 82 83 84 85 86
  //   87 c8 c9 ca cb cc cd ce cf a0 81 82 83 84 85 86 87 c8 c9 ca cb cc cd ce cf a0 81 82 83 84 85 86 87
  //   c8 c9 ca cb cc cd ce cf a0 81 82 83 84 85 86 87 c8 c9 ca cb cc cd ce cf a0 81 82 83 84 85 86 87 c8
  //   c9 ca cb cc cd ce cf a0 81 82 83 84 85 86 87 c8 c9 ca cb cc cd ce cf a0 81 82 83 84 85 86 87 c8 c9
  //   ca cb cc cd ce cf a0 81 82 83 84 85 86 87 c8 c9 ca cb cc cd ce cf a0 81 82 83 84 85 86 87 c8 c9 ca
  //   cb cc cd ce cf a0 81 82 83 84 85 86 87 c8 c9 ca cb cc cd ce cf a0 81 82 83 84 85 86 87 c8 c9 ca cb
  //   cc cd ce cf a0 81 82 83 84 85 86 87 c8 c9 ca cb cc cd ce cf a0 81 82 83 84 85 86 87 c8 c9 ca cb cc
  //   cd ce cf a0 81 82 83 84 85 86 87 c8 c9 ca cb cc cd ce cf a0 81 82 83 84 85 86 87 c8 c9 ca cb cc cd
  //   ce cf a0 81 82 83 84 85 86 87 c8 c9 ca cb cc cd ce cf a0 81 82 83 84 85 86 87 c8 c9 ca cb cc cd ce
  //   cf a0 81 82 83 84 85 86 87 c8 c9 ca cb cc cd ce cf 16*a0 16*81 16*82 16*83 16*84 16*85 16*86 16*87
  //   16*c8 16*c9 16*ca 16*cb 16*cc 16*cd 16*ce 16*cf 16*a0 16*81 16*82 16*83 16*84 16*85 16*86 16*87
  //   16*c8 16*c9 16*ca 16*cb 16*cc 16*cd 16*ce 16*cf a0 81 82 83 84 85 86 87 c8 c9 ca cb cc cd ce cf 81
  //   82 83 84 85 86 87 c8 c9 ca cb cc cd ce cf b0 82 83 84 85 86 87 c8 c9 ca cb cc cd ce cf b0 91 83 84
  //   85 86 87 c8 c9 ca cb cc cd ce cf b0 91 92 84 85 86 87 c8 c9 ca cb cc cd ce cf b0 91 92 93 85 86 87
  //   c8 c9 ca cb cc cd ce cf b0 91 92 93 94 86 87 c8 c9 ca cb cc cd ce cf b0 91 92 93 94 95 87 c8 c9 ca
  //   cb cc cd ce cf b0 91 92 93 94 95 96 c8 c9 ca cb cc cd ce cf b0 91 92 93 94 95 96 97 c9 ca cb cc cd
  //   ce cf b0 91 92 93 94 95 96 97 d8 ca cb cc cd ce cf b0 91 92 93 94 95 96 97 d8 d9 cb cc cd ce cf b0
  //   91 92 93 94 95 96 97 d8 d9 da cc cd ce cf b0 91 92 93 94 95 96 97 d8 d9 da db cd ce cf b0 91 92 93
  //   94 95 96 97 d8 d9 da db dc ce cf b0 91 92 93 94 95 96 97 d8 d9 da db dc dd cf b0 91 92 93 94 95 96
  //   97 d8 d9 da db dc dd de 20 1 2 3 4 5 6 7 48 49 4a 4b 4c 4d 4e 4f 1 2 3 4 5 6 7 48 49 4a 4b 4c 4d 4e
  //   4f 30 2 3 4 5 6 7 48 49 4a 4b 4c 4d 4e 4f 30 11 3 4 5 6 7 48 49 4a 4b 4c 4d 4e 4f 30 11 12 4 5 6 7
  //   48 49 4a 4b 4c 4d 4e 4f 30 11 12 13 5 6 7 48 49 4a 4b 4c 4d 4e 4f 30 11 12 13 14 6 7 48 49 4a 4b 4c
  //   4d 4e 4f 30 11 12 13 14 15 7 48 49 4a 4b 4c 4d 4e 4f 30 11 12 13 14 15 16 48 49 4a 4b 4c 4d 4e 4f 30
  //   11 12 13 14 15 16 17 49 4a 4b 4c 4d 4e 4f 30 11 12 13 14 15 16 17 58 4a 4b 4c 4d 4e 4f 30 11 12 13
  //   14 15 16 17 58 59 4b 4c 4d 4e 4f 30 11 12 13 14 15 16 17 58 59 5a 4c 4d 4e 4f 30 11 12 13 14 15 16
  //   17 58 59 5a 5b 4d 4e 4f 30 11 12 13 14 15 16 17 58 59 5a 5b 5c 4e 4f 30 11 12 13 14 15 16 17 58 59
  //   5a 5b 5c 5d 4f 30 11 12 13 14 15 16 17 58 59 5a 5b 5c 5d 5e b0 91 92 93 94 95 96 97 d8 d9 da db dc
  //   dd de df cf b0 91 92 93 94 95 96 97 d8 d9 da db dc dd de ce cf b0 91 92 93 94 95 96 97 d8 d9 da db
  //   dc dd cd ce cf b0 91 92 93 94 95 96 97 d8 d9 da db dc cc cd ce cf b0 91 92 93 94 95 96 97 d8 d9 da
  //   db cb cc cd ce cf b0 91 92 93 94 95 96 97 d8 d9 da ca cb cc cd ce cf b0 91 92 93 94 95 96 97 d8 d9
  //   c9 ca cb cc cd ce cf b0 91 92 93 94 95 96 97 d8 c8 c9 ca cb cc cd ce cf b0 91 92 93 94 95 96 97 87
  //   c8 c9 ca cb cc cd ce cf b0 91 92 93 94 95 96 86 87 c8 c9 ca cb cc cd ce cf b0 91 92 93 94 95 85 86
  //   87 c8 c9 ca cb cc cd ce cf b0 91 92 93 94 84 85 86 87 c8 c9 ca cb cc cd ce cf b0 91 92 93 83 84 85
  //   86 87 c8 c9 ca cb cc cd ce cf b0 91 92 82 83 84 85 86 87 c8 c9 ca cb cc cd ce cf b0 91 81 82 83 84
  //   85 86 87 c8 c9 ca cb cc cd ce cf b0 30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
  //   HIGH
  //   contents of rom_2 (hex, n*v repeats v):
  //   a0 81 82 83 84 85 86 87 c8 c9 ca cb cc cd ce cf a0 81 82 83 84 85 86 87 c8 c9 ca cb cc cd ce cf a0
  //   81 82 83 84 85 86 87 c8 c9 ca cb cc cd ce cf a0 81 82 83 84 85 86 87 c8 c9 ca cb cc cd ce cf a0 81
  //   82 83 84 85 86 87 c8 c9 ca cb cc cd ce cf a0 81 82 83 84 85 86 87 c8 c9 ca cb cc cd ce cf a0 81 82
  //   83 84 85 86 87 c8 c9 ca cb cc cd ce cf a0 81 82 83 84 85 86 87 c8 c9 ca cb cc cd ce cf a0 81 82 83
  //   84 85 86 87 c8 c9 ca cb cc cd ce cf a0 81 82 83 84 85 86 87 c8 c9 ca cb cc cd ce cf a0 81 82 83 84
  //   85 86 87 c8 c9 ca cb cc cd ce cf a0 81 82 83 84 85 86 87 c8 c9 ca cb cc cd ce cf a0 81 82 83 84 85
  //   86 87 c8 c9 ca cb cc cd ce cf a0 81 82 83 84 85 86 87 c8 c9 ca cb cc cd ce cf a0 81 82 83 84 85 86
  //   87 c8 c9 ca cb cc cd ce cf a0 81 82 83 84 85 86 87 c8 c9 ca cb cc cd ce cf a0 81 82 83 84 85 86 87
  //   c8 c9 ca cb cc cd ce cf a0 81 82 83 84 85 86 87 c8 c9 ca cb cc cd ce cf a0 81 82 83 84 85 86 87 c8
  //   c9 ca cb cc cd ce cf a0 81 82 83 84 85 86 87 c8 c9 ca cb cc cd ce cf a0 81 82 83 84 85 86 87 c8 c9
  //   ca cb cc cd ce cf a0 81 82 83 84 85 86 87 c8 c9 ca cb cc cd ce cf a0 81 82 83 84 85 86 87 c8 c9 ca
  //   cb cc cd ce cf a0 81 82 83 84 85 86 87 c8 c9 ca cb cc cd ce cf a0 81 82 83 84 85 86 87 c8 c9 ca cb
  //   cc cd ce cf a0 81 82 83 84 85 86 87 c8 c9 ca cb cc cd ce cf a0 81 82 83 84 85 86 87 c8 c9 ca cb cc
  //   cd ce cf a0 81 82 83 84 85 86 87 c8 c9 ca cb cc cd ce cf a0 81 82 83 84 85 86 87 c8 c9 ca cb cc cd
  //   ce cf a0 81 82 83 84 85 86 87 c8 c9 ca cb cc cd ce cf a0 81 82 83 84 85 86 87 c8 c9 ca cb cc cd ce
  //   cf a0 81 82 83 84 85 86 87 c8 c9 ca cb cc cd ce cf 16*a0 16*81 16*82 16*83 16*84 16*85 16*86 16*87
  //   16*c8 16*c9 16*ca 16*cb 16*cc 16*cd 16*ce 16*cf 16*a0 16*81 16*82 16*83 16*84 16*85 16*86 16*87
  //   16*c8 16*c9 16*ca 16*cb 16*cc 16*cd 16*ce 16*cf a0 81 82 83 84 85 86 87 c8 c9 ca cb cc cd ce cf 81
  //   82 83 84 85 86 87 c8 c9 ca cb cc cd ce cf b0 82 83 84 85 86 87 c8 c9 ca cb cc cd ce cf b0 91 83 84
  //   85 86 87 c8 c9 ca cb cc cd ce cf b0 91 92 84 85 86 87 c8 c9 ca cb cc cd ce cf b0 91 92 93 85 86 87
  //   c8 c9 ca cb cc cd ce cf b0 91 92 93 94 86 87 c8 c9 ca cb cc cd ce cf b0 91 92 93 94 95 87 c8 c9 ca
  //   cb cc cd ce cf b0 91 92 93 94 95 96 c8 c9 ca cb cc cd ce cf b0 91 92 93 94 95 96 97 c9 ca cb cc cd
  //   ce cf b0 91 92 93 94 95 96 97 d8 ca cb cc cd ce cf b0 91 92 93 94 95 96 97 d8 d9 cb cc cd ce cf b0
  //   91 92 93 94 95 96 97 d8 d9 da cc cd ce cf b0 91 92 93 94 95 96 97 d8 d9 da db cd ce cf b0 91 92 93
  //   94 95 96 97 d8 d9 da db dc ce cf b0 91 92 93 94 95 96 97 d8 d9 da db dc dd cf b0 91 92 93 94 95 96
  //   97 d8 d9 da db dc dd de 20 1 2 3 4 5 6 7 48 49 4a 4b 4c 4d 4e 4f 1 2 3 4 5 6 7 48 49 4a 4b 4c 4d 4e
  //   4f 30 2 3 4 5 6 7 48 49 4a 4b 4c 4d 4e 4f 30 11 3 4 5 6 7 48 49 4a 4b 4c 4d 4e 4f 30 11 12 4 5 6 7
  //   48 49 4a 4b 4c 4d 4e 4f 30 11 12 13 5 6 7 48 49 4a 4b 4c 4d 4e 4f 30 11 12 13 14 6 7 48 49 4a 4b 4c
  //   4d 4e 4f 30 11 12 13 14 15 7 48 49 4a 4b 4c 4d 4e 4f 30 11 12 13 14 15 16 48 49 4a 4b 4c 4d 4e 4f 30
  //   11 12 13 14 15 16 17 49 4a 4b 4c 4d 4e 4f 30 11 12 13 14 15 16 17 58 4a 4b 4c 4d 4e 4f 30 11 12 13
  //   14 15 16 17 58 59 4b 4c 4d 4e 4f 30 11 12 13 14 15 16 17 58 59 5a 4c 4d 4e 4f 30 11 12 13 14 15 16
  //   17 58 59 5a 5b 4d 4e 4f 30 11 12 13 14 15 16 17 58 59 5a 5b 5c 4e 4f 30 11 12 13 14 15 16 17 58 59
  //   5a 5b 5c 5d 4f 30 11 12 13 14 15 16 17 58 59 5a 5b 5c 5d 5e b0 91 92 93 94 95 96 97 d8 d9 da db dc
  //   dd de df cf b0 91 92 93 94 95 96 97 d8 d9 da db dc dd de ce cf b0 91 92 93 94 95 96 97 d8 d9 da db
  //   dc dd cd ce cf b0 91 92 93 94 95 96 97 d8 d9 da db dc cc cd ce cf b0 91 92 93 94 95 96 97 d8 d9 da
  //   db cb cc cd ce cf b0 91 92 93 94 95 96 97 d8 d9 da ca cb cc cd ce cf b0 91 92 93 94 95 96 97 d8 d9
  //   c9 ca cb cc cd ce cf b0 91 92 93 94 95 96 97 d8 c8 c9 ca cb cc cd ce cf b0 91 92 93 94 95 96 97 87
  //   c8 c9 ca cb cc cd ce cf b0 91 92 93 94 95 96 86 87 c8 c9 ca cb cc cd ce cf b0 91 92 93 94 95 85 86
  //   87 c8 c9 ca cb cc cd ce cf b0 91 92 93 94 84 85 86 87 c8 c9 ca cb cc cd ce cf b0 91 92 93 83 84 85
  //   86 87 c8 c9 ca cb cc cd ce cf b0 91 92 82 83 84 85 86 87 c8 c9 ca cb cc cd ce cf b0 91 81 82 83 84
  //   85 86 87 c8 c9 ca cb cc cd ce cf b0 30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
endmodule

module FFwithEnable (
  input  D,
  input  nen,
  input  Clk,
  input  Rst,
  output Q
);

  wire not_1_out;

  not not_1 (not_1_out, nen);
  D_Flip_Flop d_ff_1 (.clk(Clk), .D(D), .Q(Q), .en(not_1_out), .reset(Rst));  // open: Qn, preset
endmodule
